// Digital circuit BW8cpu.dig as structural Verilog
module BW8cpu (
  input  VCC,
  input  GND,
  input  nIRQ,
  input  nREQ,
  input  crystal,
  input  _555,
  input  step,
  output [15:0] ADDR,
  output R_nW,
  output nACK,
  output nBRK,
  output MEM_nIO,
  output [7:0] MemIO_Bus
);

  wire a_dbus_a, a_dbus_l, a_lhs_a, a_rhs_a, ab_xfer_l, addr_inc, addr_xfer_a, alu_dbus_a, alu_res, b_dbus_a,
       b_dbus_l, b_lhs_a, b_rhs_a, c_dbus_a, c_dbus_l, c_lhs_a, c_rhs_a, cd_xfer_l, clk, clk_crystal,
       d_dbus_a, d_dbus_l, d_lhs_a, d_rhs_a, da_dbus_a, da_dbus_l, dec_sp, dp_addr_a, dp_dbus_a, dp_dbus_l,
       ext, ir_dbus_l, isr_xfer_a, lsb_dbus_a, mem_dbus_a, mem_dbus_l, msb_dbus_a, nclk, nirq_latched,
       noffset, nreq_latched, nrst, nRST_out, off_dbus_l, pc_addr_a, pc_inc, pc_xfer_a, pc_xfer_l,
       pch_dbus_l, pcl_dbus_l, rst, sp_addr_a, sp_dec, sp_inc, sp_xfer_a, sp_xfer_l, sph_dbus_l, spl_dbus_l,
       sr_dbus_a, sr_dbus_l, t_addr_a, th_dbus_a, th_dbus_l, th_lhs_a, tl_dbus_a, tl_dbus_l, tl_rhs_a,
       x_addr_a, x_dec, x_inc, x_xfer_a, x_xfer_l, xh_dbus_l, xl_dbus_l, y_addr_a, y_dec, y_inc, y_xfer_a,
       y_xfer_l, yh_dbus_l, yl_dbus_l;
  wire [2:0] addr_a, Break_out, clk_mode, count, t_state, xfer_l;
  wire [3:0] alu_op, dbus_a;
  wire [4:0] dbus_l, flags, xfer_a;
  wire [7:0] dbus, Instruction_Register_p4, lhs, opcode, reg_a, reg_b, reg_c, reg_d, reg_da, reg_dp, reg_off,
       reg_th, reg_tl, rhs;
  wire [15:0] addr_t, reg_pc, reg_sp, reg_x, reg_y;

  ROM #(.AddrBits(16), .Bits(8), .isProgramMemory("true")) Program_ROM (.A(ADDR), .sel(1'b1), .D(MemIO_Bus));
  // Probe on dbus
  // Probe on {lhs, rhs}
  // Probe on reg_a
  // Probe on reg_b
  // Probe on reg_c
  // Probe on reg_d
  // Probe on reg_dp
  // Probe on reg_da
  // Probe on alu_res
  PowerSupply powersupply_1 (.VDD(VCC), .GND(GND));
  // Probe on addr_t
  // Probe on MemIO_Bus
  // Probe on reg_pc
  // Probe on reg_sp
  // Probe on reg_x
  // Probe on reg_y
  // Probe on reg_th
  // Probe on reg_tl
  // Probe on reg_off
  // Probe on nreq_latched
  // Probe on nirq_latched
  // Probe on opcode
  // Probe on ext
  Button u_nRST (.out(nRST_out));
  Button #(.activeLow("true")) Run (.out(Break_out[0]));
  Button #(.activeLow("true")) Demo (.out(Break_out[1]));
  Button #(.activeLow("true")) Break (.out(Break_out[2]));
  // Probe on flags
  control_unit Control_Unit (
    .nirq(nIRQ), .opcode(Instruction_Register_p4), .flags(flags), .nreq(nREQ), .clk(clk), .nrst(nrst),
    .dbus_assert(dbus_a), .dbus_load(dbus_l), .alu_op(alu_op), .xfer_assert(xfer_a), .xfer_load(xfer_l),
    .addr_assert(addr_a), .count(count), .dec_sp(dec_sp), .nbrk(nBRK), .nclk(nclk), .noffset(noffset),
    .rst(rst), .dbg({nreq_latched, nirq_latched, ext, opcode, flags, t_state}));
  // instruction_register Instruction_Register: pin names not known; wires that end beside it: dbus, ir_dbus_l, nrst, Instruction_Register_p4
  constant_generator_16bit ISR_Vector_Hi (.ISRv_Hi(16'hfe), .nASSERT_ISRvHi(isr_xfer_a), .xfer({lhs, rhs}));
  memory_bridge Memory_Bridge (.dbus_assert(mem_dbus_a), .dbus_load(mem_dbus_l), .dbus(dbus), .mbus(MemIO_Bus));
  reset_module reset_module_1 (.clk(clk_crystal), .nrst_in(nRST_out), .nrst(nrst));
  // Probe on t_state
  // triple_clock triple_clock_1: pin names not known; wires that end beside it: Break_out, nBRK, {nrst, 2'b11}, crystal, _555, step, clk, clk_crystal, clk_mode
  // Probe on nclk
  // Probe on nBRK
  LED Run_Mode_Active (.in(clk_mode[0]));
  LED Demo_Mode_Active (.in(clk_mode[1]));
  LED Break_Mode_Active (.in(clk_mode[2]));
  // Probe on dec_sp
  LED cpu (.in(clk));
  LED u_crystal (.in(clk_crystal));
  // Probe on count
  // Probe on addr_a
  // Probe on xfer_l
  // bus_controller Bus_Controller: pin names not known; wires that end beside it: dbus_a, xfer_l, addr_a, clk, count, dec_sp, nclk, dbus_l, xfer_a, alu_dbus_a, a_dbus_a, b_dbus_a, c_dbus_a, d_dbus_a, dp_dbus_a, da_dbus_a, th_dbus_a, tl_dbus_a, sr_dbus_a, mem_dbus_a, msb_dbus_a, lsb_dbus_a, a_dbus_l, b_dbus_l, c_dbus_l
  // Probe on xfer_a
  // Probe on alu_op
  // Probe on dbus_l
  // Probe on dbus_a
  // alu Arithmetic___Logic_Unit_and_Status_Register: pin names not known; wires that end beside it: alu_op, sr_dbus_l, sr_dbus_a, clk, rst, lhs, rhs, alu_dbus_a, flags, dbus, alu_res
  gpr_pair A_and_B (
    .naddr_assert(1'b1), .nxfer_load(ab_xfer_l), .nhi_dbus_load(a_dbus_l), .nlo_dbus_load(b_dbus_l),
    .nhi_dbus_assert(a_dbus_a), .nlo_dbus_assert(b_dbus_a), .nhi_lhs_assert(a_lhs_a),
    .nlo_lhs_assert(b_lhs_a), .nhi_rhs_assert(a_rhs_a), .nlo_rhs_assert(b_rhs_a), .dbus(dbus),
    .xfer({lhs, rhs}), .nclr(nrst), .reg_hi(reg_a), .reg_lo(reg_b));  // open: addr
  gpr_pair C_and_D (
    .naddr_assert(1'b1), .nxfer_load(cd_xfer_l), .nhi_dbus_load(c_dbus_l), .nlo_dbus_load(d_dbus_l),
    .nhi_dbus_assert(c_dbus_a), .nlo_dbus_assert(d_dbus_a), .nhi_lhs_assert(c_lhs_a),
    .nlo_lhs_assert(d_lhs_a), .nhi_rhs_assert(c_rhs_a), .nlo_rhs_assert(d_rhs_a), .dbus(dbus),
    .xfer({lhs, rhs}), .nclr(nrst), .reg_hi(reg_c), .reg_lo(reg_d));  // open: addr
  gpr_pair TH_and_TL (
    .naddr_assert(t_addr_a), .nxfer_load(1'b1), .nhi_dbus_load(th_dbus_l), .nlo_dbus_load(tl_dbus_l),
    .nhi_dbus_assert(th_dbus_a), .nlo_dbus_assert(tl_dbus_a), .nhi_lhs_assert(th_lhs_a),
    .nlo_lhs_assert(1'b1), .nhi_rhs_assert(1'b1), .nlo_rhs_assert(tl_rhs_a), .dbus(dbus), .xfer({lhs, rhs}),
    .nclr(nrst), .addr(addr_t), .reg_hi(reg_th), .reg_lo(reg_tl));
  gpr_pair DP_and_DA (
    .naddr_assert(dp_addr_a), .nxfer_load(1'b1), .nhi_dbus_load(dp_dbus_l), .nlo_dbus_load(da_dbus_l),
    .nhi_dbus_assert(dp_dbus_a), .nlo_dbus_assert(da_dbus_a), .nhi_lhs_assert(1'b1), .nlo_lhs_assert(1'b1),
    .nhi_rhs_assert(1'b1), .nlo_rhs_assert(1'b1), .dbus(dbus), .xfer({lhs, rhs}), .nclr(nrst), .addr(addr_t),
    .reg_hi(reg_dp), .reg_lo(reg_da));
  address_register Program_Counter (
    .xfer({lhs, rhs}), .clr(rst), .nxfer_load(pc_xfer_l), .naddr_assert(pc_addr_a), .nxfer_assert(pc_xfer_a),
    .inc(pc_inc), .dec(1'b1), .clk(clk), .nhi_dbus_load(pch_dbus_l), .nlo_dbus_load(pcl_dbus_l), .dbus(dbus),
    .addr(addr_t), .\reg (reg_pc));
  address_register Stack_Pointer (
    .xfer({lhs, rhs}), .clr(rst), .nxfer_load(sp_xfer_l), .naddr_assert(sp_addr_a), .nxfer_assert(sp_xfer_a),
    .inc(sp_inc), .dec(sp_dec), .clk(clk), .nhi_dbus_load(sph_dbus_l), .nlo_dbus_load(spl_dbus_l),
    .dbus(dbus), .addr(addr_t), .\reg (reg_sp));
  address_register X_Index (
    .xfer({lhs, rhs}), .clr(rst), .nxfer_load(x_xfer_l), .naddr_assert(x_addr_a), .nxfer_assert(x_xfer_a),
    .inc(x_inc), .dec(x_dec), .clk(clk), .nhi_dbus_load(xh_dbus_l), .nlo_dbus_load(xl_dbus_l), .dbus(dbus),
    .addr(addr_t), .\reg (reg_x));
  address_register Y_Index (
    .xfer({lhs, rhs}), .clr(rst), .nxfer_load(y_xfer_l), .naddr_assert(y_addr_a), .nxfer_assert(y_xfer_a),
    .inc(y_inc), .dec(y_dec), .clk(clk), .nhi_dbus_load(yh_dbus_l), .nlo_dbus_load(yl_dbus_l), .dbus(dbus),
    .addr(addr_t), .\reg (reg_y));
  address_offset Address_Bridge (
    .nclk(off_dbus_l), .dbus(dbus), .addr_in(addr_t), .noffset_en(noffset), .carry_en(addr_inc),
    .naddr_xfer_assert(addr_xfer_a), .nassert_addr(nACK), .nclr(nrst), .addr_out(ADDR), .xfer({lhs, rhs}),
    .q(reg_off));

  assign R_nW = 1'b0;

  // Other names for the same wires on the sheet: ack_addr_a = nACK; addr_out[15:0] = ADDR; clk_cpu = clk;
  //   io_addr_a = MEM_nIO; mbus[7:0] = MemIO_Bus; rst_clk_mode[2] = nrst; xfer[15:0] = {lhs, rhs}

  // Notes on the sheet:
  //   VCC: default 1
  //   nIRQ: default 1
  //   nREQ: default 1
  //   crystal: Hz: 5
  //   Program_ROM loads foo.bin
  //   External Pinout
  //   Buses & Constants
  //   Registers
endmodule
