// Digital circuit control_unit.dig as structural Verilog
module control_unit (
  input  nirq,
  input  [7:0] opcode,
  input  [4:0] flags,
  input  nreq,
  input  clk,
  input  nrst,
  output [3:0] dbus_assert,
  output [3:0] dbus_load,
  output [4:0] alu_op,
  output [4:0] xfer_assert,
  output [2:0] xfer_load,
  output [2:0] addr_assert,
  output [2:0] count,
  output dec_sp,
  output nbrk,
  output nclk,
  output rst,
  output [18:0] dbg
);

  wire brk, notconnected_1_out, notconnected_2_out, notconnected_3_out, notconnected_4_out,
       notconnected_5_out, nrst_latch, nrst_useq, or_1_out, or_2_out, rst_useq;
  wire [0:0] rs_ff_as_1_q;
  wire [1:0] m_tog;
  wire [7:0] ucode0_d, ucode1_d, ucode2_d, ucode3_d;
  wire [7:1] Interrupt_Latch_q;

  // NotConnected on notconnected_1_out
  RS_FF_AS rs_ff_as_1 (.S(rst), .R(nrst_useq), .Q(rs_ff_as_1_q[0]));  // open: nQ
  // _7404 clk_inverter: pin names not known; wires that end beside it: clk, nrst, brk, nrst_useq, dbg[18], notconnected_1_out, 1'b1, 1'b0, nclk, rst, nbrk, rst_useq, nrst_latch
  _74ls273 Interrupt_Latch (
    .CP(clk), .nMR(nrst), .D({4'b0000, nirq, 2'b00, rs_ff_as_1_q[0]}), .VCC(1'b1), .GND(1'b0),
    .Q({Interrupt_Latch_q[7:4], dbg[17], Interrupt_Latch_q[2:1], dbg[18]}));
  or or_1 (or_1_out, rst_useq, rst);
  or or_2 (or_2_out, or_1_out, nrst_latch);
  // NotConnected on notconnected_2_out
  // NotConnected on notconnected_3_out
  // NotConnected on notconnected_4_out
  // NotConnected on notconnected_5_out
  // _74193 sequencer: pin names not known; wires that end beside it: notconnected_2_out, 1'b1, clk, notconnected_3_out, notconnected_4_out, notconnected_5_out, or_2_out, 1'b1, 1'b1, 1'b0, dbg[0], dbg[1], dbg[2]
  ROM #(.AddrBits(19), .Bits(8)) ucode0 (.A({dbg[18:17], 1'b0, opcode, flags, dbg[2:0]}), .sel(1'b1), .D(ucode0_d));
  ROM #(.AddrBits(19), .Bits(8)) ucode1 (.A({dbg[18:17], 1'b0, opcode, flags, dbg[2:0]}), .sel(1'b1), .D(ucode1_d));
  ROM #(.AddrBits(19), .Bits(8)) ucode2 (.A({dbg[18:17], 1'b0, opcode, flags, dbg[2:0]}), .sel(1'b1), .D(ucode2_d));
  ROM #(.AddrBits(19), .Bits(8)) ucode3 (.A({dbg[18:17], 1'b0, opcode, flags, dbg[2:0]}), .sel(1'b1), .D(ucode3_d));
  _74ls273 _74ls273_1 (.CP(clk), .nMR(nrst), .D(ucode0_d), .VCC(1'b1), .GND(1'b0), .Q({dbus_load, dbus_assert}));
  _74ls273 _74ls273_2 (.CP(clk), .nMR(nrst), .D(ucode1_d), .VCC(1'b1), .GND(1'b0), .Q({xfer_assert[2:0], alu_op}));
  _74ls273 _74ls273_3 (
    .CP(clk), .nMR(nrst), .D(ucode2_d), .VCC(1'b1), .GND(1'b0), .Q({addr_assert, xfer_load, xfer_assert[4:3]}));
  _74ls273 _74ls273_4 (
    .CP(clk), .nMR(nrst), .D(ucode3_d), .VCC(1'b1), .GND(1'b0), .Q({brk, m_tog, nrst_useq, dec_sp, count}));

  assign dbg[16:3] = {1'b0, opcode, flags};

  // Other names for the same wires on the sheet: xa_3 = xfer_assert[3]; xa_4 = xfer_assert[4]; xa_0 = xfer_assert[0];
  //   xa_1 = xfer_assert[1]; xa_2 = xfer_assert[2]; t_state[2:0] = dbg[2:0];
  //   ucode_addr (some bits) = {dbg[18:17], opcode, flags, dbg[2:0]}; rst_latch = dbg[18]; nirq_latch = dbg[17]

  // Notes on the sheet:
  //   ucode0 loads control_0.bin
  //   ucode1 loads control_1.bin
  //   ucode2 loads control_2.bin
  //   ucode3 loads control_3.bin
endmodule
